# Fritzing sketch Monitoring_K3s (saved by Fritzing 1.0.1rc)
breadboards: 1

parts:
  U1 = ESP8266 NodeMCU LoLin module
  LEDServerUp = LED - 5mm [color="Green (555nm)" current=0.030A package="5 mm [THT]"]
  LEDServerDown = LED - 5mm [color="Red (633nm)" current=0.030A package="5 mm [THT]"]
  V2 = DC Power [voltage=5]  # not connected
  LEDClusterUp = LED - 5mm [color="Green (555nm)" current=0.030A package="5 mm [THT]"]
  LEDClusterDown = LED - 5mm [color="Red (633nm)" current=0.030A package="5 mm [THT]"]
  LEDAppUp = LED - 5mm [color="Green (555nm)" current=0.030A package="5 mm [THT]"]
  LEDAppDown = LED - 5mm [color="Red (633nm)" current=0.030A package="5 mm [THT]"]
  RServerDown = Resistor [tolerance=±5% power=0.25W resistance=220 package=THT]
  RServerUp = Resistor [tolerance=±5% power=0.25W resistance=220 package=THT]
  RClusterDown = Resistor [tolerance=±5% power=0.25W resistance=220 package=THT]
  RClusterUp = Resistor [tolerance=±5% power=0.25W resistance=220 package=THT]
  RAppDown = Resistor [tolerance=±5% power=0.25W resistance=220 package=THT]
  RAppUp = Resistor [tolerance=±5% power=0.25W resistance=220 package=THT]

nets:
  N1: U1.D1, RServerDown.Pin_0
  N2: U1.D2, RServerUp.Pin_0
  N3: U1.D3, RClusterDown.Pin_0
  N4: U1.D4, RClusterUp.Pin_0
  N5: U1.GND, LEDServerUp.cathode, LEDServerDown.cathode, LEDClusterUp.cathode, LEDClusterDown.cathode, LEDAppUp.cathode, LEDAppDown.cathode
  N6: U1.D5, RAppDown.Pin_0
  N7: U1.D6, RAppUp.Pin_0
  N8: LEDServerUp.anode, RServerUp.Pin_1
  N9: LEDServerDown.anode, RServerDown.Pin_1
  N10: LEDClusterUp.anode, RClusterUp.Pin_1
  N11: LEDClusterDown.anode, RClusterDown.Pin_1
  N12: LEDAppUp.anode, RAppUp.Pin_1
  N13: LEDAppDown.anode, RAppDown.Pin_1

custom parts:
  ESP8266 NodeMCU LoLin module: ESP8266 based NodeMCU
